// Logisim project 16_bitlatch.circ as structural Verilog: 1 circuit, main circuit main
module main (
  input  in_1,
  input  in_2,
  input  in_3,
  input  in_4,
  input  in_5,
  input  in_6,
  input  in_7,
  input  in_8,
  input  in_9,
  input  in_10,
  input  in_11,
  input  in_12,
  input  in_13,
  input  in_14,
  input  in_15,
  input  in_16,
  input  Enable
);

  wire and_1_out, and_2_out, and_3_out, and_4_out, and_5_out, and_6_out, and_7_out, and_8_out, and_9_out,
       and_10_out, and_11_out, and_12_out, and_13_out, and_14_out, and_15_out, and_16_out, and_17_out,
       and_18_out, and_19_out, and_20_out, and_21_out, and_22_out, and_23_out, and_24_out, and_25_out,
       and_26_out, and_27_out, and_28_out, and_29_out, and_30_out, and_31_out, and_32_out, and_33_out,
       and_34_out, and_35_out, and_36_out, and_37_out, and_38_out, and_39_out, and_40_out, and_41_out,
       and_42_out, and_43_out, and_44_out, and_45_out, and_46_out, and_47_out, and_48_out, and_49_out,
       and_50_out, and_51_out, and_52_out, and_53_out, and_54_out, and_55_out, and_56_out, and_57_out,
       and_58_out, and_59_out, and_60_out, and_61_out, and_62_out, and_63_out, and_64_out, not_1_out,
       not_2_out, not_3_out, not_4_out, not_5_out, not_6_out, not_7_out, not_8_out, not_9_out, not_10_out,
       not_11_out, not_12_out, not_13_out, not_14_out, not_15_out, not_16_out, not_17_out, not_18_out,
       not_19_out, not_20_out, not_21_out, not_22_out, not_23_out, not_24_out, not_25_out, not_26_out,
       not_27_out, not_28_out, not_29_out, not_30_out, not_31_out, not_32_out, not_33_out, not_34_out,
       not_35_out, not_36_out, not_37_out, not_38_out, not_39_out, not_40_out, not_41_out, not_42_out,
       not_43_out, not_44_out, not_45_out, not_46_out, not_47_out, not_48_out, not_49_out, not_50_out,
       not_51_out, not_52_out, not_53_out, not_54_out, not_55_out, not_56_out, not_57_out, not_58_out,
       not_59_out, not_60_out, not_61_out, not_62_out, not_63_out, not_64_out, not_65_out, not_66_out,
       not_67_out, not_68_out, not_69_out, not_70_out, not_71_out, not_72_out, not_73_out, not_74_out,
       not_75_out, not_76_out, not_77_out, not_78_out, not_79_out, not_80_out;

  LED led_1 (.in(not_49_out));
  LED led_2 (.in(not_51_out));
  LED led_3 (.in(not_53_out));
  not not_1 (not_1_out, in_1);
  not not_2 (not_2_out, in_2);
  not not_3 (not_3_out, in_3);
  not not_4 (not_4_out, in_4);
  not not_5 (not_5_out, in_5);
  not not_6 (not_6_out, in_6);
  not not_7 (not_7_out, in_7);
  not not_8 (not_8_out, in_8);
  not not_9 (not_9_out, in_9);
  not not_10 (not_10_out, in_10);
  not not_11 (not_11_out, in_11);
  not not_12 (not_12_out, in_12);
  not not_13 (not_13_out, in_13);
  not not_14 (not_14_out, in_14);
  not not_15 (not_15_out, in_15);
  not not_16 (not_16_out, in_16);
  LED led_4 (.in(not_55_out));
  LED led_5 (.in(not_57_out));
  and and_1 (and_1_out, in_1, Enable);
  and and_2 (and_2_out, Enable, not_1_out);
  and and_3 (and_3_out, in_2, Enable);
  and and_4 (and_4_out, Enable, not_2_out);
  and and_5 (and_5_out, in_3, Enable);
  and and_6 (and_6_out, Enable, not_3_out);
  and and_7 (and_7_out, in_4, Enable);
  and and_8 (and_8_out, Enable, not_4_out);
  and and_9 (and_9_out, in_5, Enable);
  and and_10 (and_10_out, Enable, not_5_out);
  and and_11 (and_11_out, in_6, Enable);
  and and_12 (and_12_out, Enable, not_6_out);
  and and_13 (and_13_out, in_7, Enable);
  and and_14 (and_14_out, Enable, not_7_out);
  and and_15 (and_15_out, in_8, Enable);
  and and_16 (and_16_out, Enable, not_8_out);
  and and_17 (and_17_out, in_9, Enable);
  and and_18 (and_18_out, Enable, not_9_out);
  and and_19 (and_19_out, in_10, Enable);
  and and_20 (and_20_out, Enable, not_10_out);
  and and_21 (and_21_out, in_11, Enable);
  and and_22 (and_22_out, Enable, not_11_out);
  and and_23 (and_23_out, in_12, Enable);
  and and_24 (and_24_out, Enable, not_12_out);
  and and_25 (and_25_out, in_13, Enable);
  and and_26 (and_26_out, Enable, not_13_out);
  and and_27 (and_27_out, in_14, Enable);
  and and_28 (and_28_out, Enable, not_14_out);
  and and_29 (and_29_out, in_15, Enable);
  and and_30 (and_30_out, Enable, not_15_out);
  and and_31 (and_31_out, in_16, Enable);
  and and_32 (and_32_out, Enable, not_16_out);
  LED led_6 (.in(not_59_out));
  LED led_7 (.in(not_61_out));
  LED led_8 (.in(not_63_out));
  not not_17 (not_17_out, and_1_out);
  not not_18 (not_18_out, and_2_out);
  not not_19 (not_19_out, and_3_out);
  not not_20 (not_20_out, and_4_out);
  not not_21 (not_21_out, and_5_out);
  not not_22 (not_22_out, and_6_out);
  not not_23 (not_23_out, and_7_out);
  not not_24 (not_24_out, and_8_out);
  not not_25 (not_25_out, and_9_out);
  not not_26 (not_26_out, and_10_out);
  not not_27 (not_27_out, and_11_out);
  not not_28 (not_28_out, and_12_out);
  not not_29 (not_29_out, and_13_out);
  not not_30 (not_30_out, and_14_out);
  not not_31 (not_31_out, and_15_out);
  not not_32 (not_32_out, and_16_out);
  not not_33 (not_33_out, and_17_out);
  not not_34 (not_34_out, and_18_out);
  not not_35 (not_35_out, and_19_out);
  not not_36 (not_36_out, and_20_out);
  not not_37 (not_37_out, and_21_out);
  not not_38 (not_38_out, and_22_out);
  not not_39 (not_39_out, and_23_out);
  not not_40 (not_40_out, and_24_out);
  not not_41 (not_41_out, and_25_out);
  not not_42 (not_42_out, and_26_out);
  not not_43 (not_43_out, and_27_out);
  not not_44 (not_44_out, and_28_out);
  not not_45 (not_45_out, and_29_out);
  not not_46 (not_46_out, and_30_out);
  not not_47 (not_47_out, and_31_out);
  not not_48 (not_48_out, and_32_out);
  LED led_9 (.in(not_67_out));
  LED led_10 (.in(not_65_out));
  LED led_11 (.in(not_69_out));
  and and_33 (and_33_out, not_17_out, not_50_out);
  LED led_12 (.in(not_71_out));
  LED led_13 (.in(not_73_out));
  not not_49 (not_49_out, and_33_out);
  and and_34 (and_34_out, not_49_out, not_18_out);
  not not_50 (not_50_out, and_34_out);
  not not_51 (not_51_out, and_35_out);
  and and_35 (and_35_out, not_19_out, not_52_out);
  and and_36 (and_36_out, not_51_out, not_20_out);
  not not_52 (not_52_out, and_36_out);
  not not_53 (not_53_out, and_37_out);
  and and_37 (and_37_out, not_21_out, not_54_out);
  not not_54 (not_54_out, and_38_out);
  and and_38 (and_38_out, not_53_out, not_22_out);
  and and_39 (and_39_out, not_23_out, not_56_out);
  not not_55 (not_55_out, and_39_out);
  not not_56 (not_56_out, and_40_out);
  and and_40 (and_40_out, not_55_out, not_24_out);
  and and_41 (and_41_out, not_25_out, not_58_out);
  not not_57 (not_57_out, and_41_out);
  not not_58 (not_58_out, and_42_out);
  and and_42 (and_42_out, not_57_out, not_26_out);
  not not_59 (not_59_out, and_43_out);
  and and_43 (and_43_out, not_27_out, not_60_out);
  and and_44 (and_44_out, not_59_out, not_28_out);
  not not_60 (not_60_out, and_44_out);
  not not_61 (not_61_out, and_45_out);
  and and_45 (and_45_out, not_29_out, not_62_out);
  and and_46 (and_46_out, not_61_out, not_30_out);
  not not_62 (not_62_out, and_46_out);
  and and_47 (and_47_out, not_31_out, not_64_out);
  not not_63 (not_63_out, and_47_out);
  and and_48 (and_48_out, not_63_out, not_32_out);
  not not_64 (not_64_out, and_48_out);
  not not_65 (not_65_out, and_49_out);
  and and_49 (and_49_out, not_33_out, not_66_out);
  not not_66 (not_66_out, and_50_out);
  and and_50 (and_50_out, not_65_out, not_34_out);
  not not_67 (not_67_out, and_51_out);
  and and_51 (and_51_out, not_35_out, not_68_out);
  and and_52 (and_52_out, not_67_out, not_67_out, not_36_out);
  not not_68 (not_68_out, and_52_out);
  not not_69 (not_69_out, and_53_out);
  and and_53 (and_53_out, not_37_out, not_70_out);
  not not_70 (not_70_out, and_54_out);
  and and_54 (and_54_out, not_69_out, not_69_out, not_38_out);
  and and_55 (and_55_out, not_39_out, not_72_out);
  not not_71 (not_71_out, and_55_out);
  and and_56 (and_56_out, not_71_out, not_40_out);
  not not_72 (not_72_out, and_56_out);
  and and_57 (and_57_out, not_41_out, not_74_out);
  not not_73 (not_73_out, and_57_out);
  not not_74 (not_74_out, and_58_out);
  and and_58 (and_58_out, not_73_out, not_42_out);
  not not_75 (not_75_out, and_59_out);
  and and_59 (and_59_out, not_43_out, not_76_out);
  not not_76 (not_76_out, and_60_out);
  and and_60 (and_60_out, not_75_out, not_44_out);
  not not_77 (not_77_out, and_61_out);
  and and_61 (and_61_out, not_45_out, not_78_out);
  not not_78 (not_78_out, and_62_out);
  and and_62 (and_62_out, not_77_out, not_46_out);
  and and_63 (and_63_out, not_47_out, not_80_out);
  not not_79 (not_79_out, and_63_out);
  not not_80 (not_80_out, and_64_out);
  and and_64 (and_64_out, not_79_out, not_48_out);
  LED led_14 (.in(not_79_out));
  LED led_15 (.in(not_77_out));
  LED led_16 (.in(not_75_out));

  // Notes on the sheet:
  //   16 Bit input Pins
  //   Output LED
endmodule
