// Logisim project 4-1 multiplexer_v2.circ as structural Verilog: 1 circuit, main circuit main
module main (
  input  S0,
  input  S1,
  input  I0,
  input  I0_2,
  input  I0_3,
  input  I0_4,
  input  I1,
  input  I1_2,
  input  I1_3,
  input  I1_4,
  input  I2,
  input  I2_2,
  input  I2_3,
  input  I2_4,
  input  I3,
  input  I3_2,
  input  I3_3,
  input  I3_4,
  input  I4,
  input  I4_2,
  input  I4_3,
  input  I4_4,
  input  I5,
  input  I5_2,
  input  I5_3,
  input  I5_4,
  input  I6,
  input  I6_2,
  input  I6_3,
  input  I6_4,
  input  I7,
  input  I7_2,
  input  I7_3,
  input  I7_4,
  input  I8,
  input  I8_2,
  input  I8_3,
  input  I8_4,
  input  I9,
  input  I9_2,
  input  I9_3,
  input  I9_4,
  input  I10,
  input  I10_2,
  input  I10_3,
  input  I10_4,
  input  I11,
  input  I11_2,
  input  I11_3,
  input  I11_4,
  input  I12,
  input  I12_2,
  input  I12_3,
  input  I12_4,
  input  I13,
  input  I13_2,
  input  I13_3,
  input  I13_4,
  input  I14,
  input  I14_2,
  input  I14_3,
  input  I14_4,
  input  I15,
  input  I15_2,
  input  I15_3,
  input  I15_4
);

  wire and_1_out, and_2_out, and_3_out, and_4_out, and_5_out, and_6_out, and_7_out, and_8_out, and_9_out,
       and_10_out, and_11_out, and_12_out, and_13_out, and_14_out, and_15_out, and_16_out, and_17_out,
       and_18_out, and_19_out, and_20_out, and_21_out, and_22_out, and_23_out, and_24_out, and_25_out,
       and_26_out, and_27_out, and_28_out, and_29_out, and_30_out, and_31_out, and_32_out, and_33_out,
       and_34_out, and_35_out, and_36_out, and_37_out, and_38_out, and_39_out, and_40_out, and_41_out,
       and_42_out, and_43_out, and_44_out, and_45_out, and_46_out, and_47_out, and_48_out, and_49_out,
       and_50_out, and_51_out, and_52_out, and_53_out, and_54_out, and_55_out, and_56_out, and_57_out,
       and_58_out, and_59_out, and_60_out, and_61_out, and_62_out, and_63_out, and_64_out, not_1_out,
       not_2_out, not_3_out, not_4_out, not_5_out, not_6_out, not_7_out, not_8_out, not_9_out, not_10_out,
       not_11_out, not_12_out, not_13_out, not_14_out, not_15_out, not_16_out, not_17_out, not_18_out,
       not_19_out, not_20_out, not_21_out, not_22_out, not_23_out, not_24_out, not_25_out, not_26_out,
       not_27_out, not_28_out, not_29_out, not_30_out, not_31_out, not_32_out, or_1_out, or_2_out, or_3_out,
       or_4_out, or_5_out, or_6_out, or_7_out, or_8_out, or_9_out, or_10_out, or_11_out, or_12_out,
       or_13_out, or_14_out, or_15_out, or_16_out;

  not not_1 (not_1_out, S0);
  not not_2 (not_2_out, S1);
  not not_3 (not_3_out, S0);
  not not_4 (not_4_out, S1);
  not not_5 (not_5_out, S0);
  not not_6 (not_6_out, S1);
  not not_7 (not_7_out, S0);
  not not_8 (not_8_out, S1);
  and and_1 (and_1_out, not_1_out, I0, not_2_out);
  and and_2 (and_2_out, not_1_out, I1, S1);
  and and_3 (and_3_out, I2, S0, not_2_out);
  and and_4 (and_4_out, S0, S1, I3);
  and and_5 (and_5_out, not_3_out, I4, not_4_out);
  and and_6 (and_6_out, not_3_out, I5, S1);
  and and_7 (and_7_out, I6, S0, not_4_out);
  and and_8 (and_8_out, S0, S1, I7);
  and and_9 (and_9_out, not_5_out, I8, not_6_out);
  and and_10 (and_10_out, not_5_out, I9, S1);
  and and_11 (and_11_out, I10, S0, not_6_out);
  and and_12 (and_12_out, S0, S1, I11);
  and and_13 (and_13_out, not_7_out, I12, not_8_out);
  and and_14 (and_14_out, not_7_out, I13, S1);
  and and_15 (and_15_out, I14, S0, not_8_out);
  and and_16 (and_16_out, S0, S1, I15);
  LED led_1 (.in(or_1_out));
  or or_1 (or_1_out, and_1_out, and_2_out, and_3_out, and_4_out);
  or or_2 (or_2_out, and_5_out, and_6_out, and_7_out, and_8_out);
  or or_3 (or_3_out, and_9_out, and_10_out, and_11_out, and_12_out);
  or or_4 (or_4_out, and_13_out, and_14_out, and_15_out, and_16_out);
  LED led_2 (.in(or_4_out));
  LED led_3 (.in(or_2_out));
  LED led_4 (.in(or_3_out));
  LED led_5 (.in(or_6_out));
  LED led_6 (.in(or_8_out));
  LED led_7 (.in(or_5_out));
  LED led_8 (.in(or_7_out));
  LED led_9 (.in(or_11_out));
  LED led_10 (.in(or_10_out));
  LED led_11 (.in(or_9_out));
  LED led_12 (.in(or_12_out));
  LED led_13 (.in(or_16_out));
  LED led_14 (.in(or_14_out));
  LED led_15 (.in(or_15_out));
  LED led_16 (.in(or_13_out));
  not not_9 (not_9_out, S1);
  not not_10 (not_10_out, S1);
  not not_11 (not_11_out, S1);
  not not_12 (not_12_out, S1);
  not not_13 (not_13_out, S0);
  not not_14 (not_14_out, S0);
  not not_15 (not_15_out, S0);
  not not_16 (not_16_out, S0);
  and and_17 (and_17_out, not_13_out, I0_2, not_9_out);
  and and_18 (and_18_out, not_13_out, I1_2, S1);
  and and_19 (and_19_out, I2_2, S0, not_9_out);
  and and_20 (and_20_out, S0, S1, I3_2);
  and and_21 (and_21_out, not_14_out, I4_2, not_10_out);
  and and_22 (and_22_out, not_14_out, I5_2, S1);
  and and_23 (and_23_out, I6_2, S0, not_10_out);
  and and_24 (and_24_out, S0, S1, I7_2);
  and and_25 (and_25_out, not_15_out, I8_2, not_11_out);
  and and_26 (and_26_out, not_15_out, I9_2, S1);
  and and_27 (and_27_out, I10_2, S0, not_11_out);
  and and_28 (and_28_out, S0, S1, I11_2);
  and and_29 (and_29_out, not_16_out, I12_2, not_12_out);
  and and_30 (and_30_out, not_16_out, I13_2, S1);
  and and_31 (and_31_out, I14_2, S0, not_12_out);
  and and_32 (and_32_out, S0, S1, I15_2);
  or or_5 (or_5_out, and_17_out, and_18_out, and_19_out, and_20_out);
  or or_6 (or_6_out, and_21_out, and_22_out, and_23_out, and_24_out);
  or or_7 (or_7_out, and_25_out, and_26_out, and_27_out, and_28_out);
  or or_8 (or_8_out, and_29_out, and_30_out, and_31_out, and_32_out);
  not not_17 (not_17_out, S0);
  not not_18 (not_18_out, S1);
  not not_19 (not_19_out, S0);
  not not_20 (not_20_out, S1);
  not not_21 (not_21_out, S0);
  not not_22 (not_22_out, S1);
  not not_23 (not_23_out, S0);
  not not_24 (not_24_out, S1);
  and and_33 (and_33_out, not_17_out, I0_3, not_18_out);
  and and_34 (and_34_out, not_17_out, I1_3, S1);
  and and_35 (and_35_out, I2_3, S0, not_18_out);
  and and_36 (and_36_out, S0, S1, I3_3);
  and and_37 (and_37_out, not_19_out, I4_3, not_20_out);
  and and_38 (and_38_out, not_19_out, I5_3, S1);
  and and_39 (and_39_out, I6_3, S0, not_20_out);
  and and_40 (and_40_out, S0, S1, I7_3);
  and and_41 (and_41_out, not_21_out, I8_3, not_22_out);
  and and_42 (and_42_out, not_21_out, I9_3, S1);
  and and_43 (and_43_out, I10_3, S0, not_22_out);
  and and_44 (and_44_out, S0, S1, I11_3);
  and and_45 (and_45_out, not_23_out, I12_3, not_24_out);
  and and_46 (and_46_out, not_23_out, I13_3, S1);
  and and_47 (and_47_out, I14_3, S0, not_24_out);
  and and_48 (and_48_out, S0, S1, I15_3);
  or or_9 (or_9_out, and_33_out, and_34_out, and_35_out, and_36_out);
  or or_10 (or_10_out, and_37_out, and_38_out, and_39_out, and_40_out);
  or or_11 (or_11_out, and_41_out, and_42_out, and_43_out, and_44_out);
  or or_12 (or_12_out, and_45_out, and_46_out, and_47_out, and_48_out);
  not not_25 (not_25_out, S1);
  not not_26 (not_26_out, S1);
  not not_27 (not_27_out, S1);
  not not_28 (not_28_out, S1);
  not not_29 (not_29_out, S0);
  not not_30 (not_30_out, S0);
  not not_31 (not_31_out, S0);
  not not_32 (not_32_out, S0);
  and and_49 (and_49_out, not_29_out, I0_4, not_25_out);
  and and_50 (and_50_out, not_29_out, I1_4, S1);
  and and_51 (and_51_out, I2_4, S0, not_25_out);
  and and_52 (and_52_out, S0, S1, I3_4);
  and and_53 (and_53_out, not_30_out, I4_4, not_26_out);
  and and_54 (and_54_out, not_30_out, I5_4, S1);
  and and_55 (and_55_out, I6_4, S0, not_26_out);
  and and_56 (and_56_out, S0, S1, I7_4);
  and and_57 (and_57_out, not_31_out, I8_4, not_27_out);
  and and_58 (and_58_out, not_31_out, I9_4, S1);
  and and_59 (and_59_out, I10_4, S0, not_27_out);
  and and_60 (and_60_out, S0, S1, I11_4);
  and and_61 (and_61_out, not_32_out, I12_4, not_28_out);
  and and_62 (and_62_out, not_32_out, I13_4, S1);
  and and_63 (and_63_out, I14_4, S0, not_28_out);
  and and_64 (and_64_out, S0, S1, I15_4);
  or or_13 (or_13_out, and_49_out, and_50_out, and_51_out, and_52_out);
  or or_14 (or_14_out, and_53_out, and_54_out, and_55_out, and_56_out);
  or or_15 (or_15_out, and_57_out, and_58_out, and_59_out, and_60_out);
  or or_16 (or_16_out, and_61_out, and_62_out, and_63_out, and_64_out);
endmodule
