// Logisim project 9 bit latch.circ as structural Verilog: 1 circuit, main circuit main
module main (
  input  in_1,
  input  in_2,
  input  in_3,
  input  in_4,
  input  in_5,
  input  in_6,
  input  in_7,
  input  in_8,
  input  in_9,
  input  in_10
);

  wire and_1_out, and_2_out, and_3_out, and_4_out, and_5_out, and_6_out, and_7_out, and_8_out, and_9_out,
       and_10_out, and_11_out, and_12_out, and_13_out, and_14_out, and_15_out, and_16_out, and_17_out,
       and_18_out, nor_1_out, nor_2_out, nor_3_out, nor_4_out, nor_5_out, nor_6_out, nor_7_out, nor_8_out,
       nor_9_out, nor_10_out, nor_11_out, nor_12_out, nor_13_out, nor_14_out, nor_15_out, nor_16_out,
       nor_17_out, nor_18_out, not_1_out, not_2_out, not_3_out, not_4_out, not_5_out, not_6_out, not_7_out,
       not_8_out, not_9_out;

  not not_1 (not_1_out, in_2);
  not not_2 (not_2_out, in_3);
  not not_3 (not_3_out, in_4);
  not not_4 (not_4_out, in_5);
  not not_5 (not_5_out, in_6);
  not not_6 (not_6_out, in_7);
  not not_7 (not_7_out, in_8);
  not not_8 (not_8_out, in_9);
  not not_9 (not_9_out, in_10);
  and and_1 (and_1_out, not_1_out, in_1);
  and and_2 (and_2_out, in_1, in_2);
  and and_3 (and_3_out, not_2_out, in_1);
  and and_4 (and_4_out, in_1, in_3);
  and and_5 (and_5_out, not_3_out, in_1);
  and and_6 (and_6_out, in_1, in_4);
  and and_7 (and_7_out, not_4_out, in_1);
  and and_8 (and_8_out, in_1, in_5);
  and and_9 (and_9_out, not_5_out, in_1);
  and and_10 (and_10_out, in_1, in_6);
  and and_11 (and_11_out, not_6_out, in_1);
  and and_12 (and_12_out, in_1, in_7);
  and and_13 (and_13_out, not_7_out, in_1);
  and and_14 (and_14_out, in_1, in_8);
  and and_15 (and_15_out, not_8_out, in_1);
  and and_16 (and_16_out, in_1, in_9);
  and and_17 (and_17_out, not_9_out, in_1);
  and and_18 (and_18_out, in_1, in_10);
  nor nor_1 (nor_1_out, and_5_out, nor_2_out);
  nor nor_2 (nor_2_out, nor_1_out, and_6_out);
  nor nor_3 (nor_3_out, and_11_out, nor_4_out);
  nor nor_4 (nor_4_out, nor_3_out, and_12_out);
  nor nor_5 (nor_5_out, and_17_out, nor_6_out);
  nor nor_6 (nor_6_out, nor_5_out, and_18_out);
  nor nor_7 (nor_7_out, and_1_out, nor_8_out);
  nor nor_8 (nor_8_out, nor_7_out, and_2_out);
  nor nor_9 (nor_9_out, and_3_out, nor_10_out);
  nor nor_10 (nor_10_out, nor_9_out, and_4_out, and_4_out);
  nor nor_11 (nor_11_out, and_7_out, nor_12_out);
  nor nor_12 (nor_12_out, nor_11_out, and_8_out);
  nor nor_13 (nor_13_out, and_9_out, nor_14_out);
  nor nor_14 (nor_14_out, nor_13_out, and_10_out, and_10_out);
  nor nor_15 (nor_15_out, and_13_out, nor_16_out);
  nor nor_16 (nor_16_out, nor_15_out, and_14_out);
  nor nor_17 (nor_17_out, and_15_out, nor_18_out);
  nor nor_18 (nor_18_out, nor_17_out, and_16_out, and_16_out);
  LED led_1 (.in(nor_7_out));
  LED led_2 (.in(nor_9_out));
  LED led_3 (.in(nor_1_out));
  LED led_4 (.in(nor_11_out));
  LED led_5 (.in(nor_13_out));
  LED led_6 (.in(nor_3_out));
  LED led_7 (.in(nor_15_out));
  LED led_8 (.in(nor_17_out));
  LED led_9 (.in(nor_5_out));
endmodule
