// Logisim project ALU_desgin.circ as structural Verilog: 1 circuit, main circuit main
module main (
  input  in_1,
  input  in_2,
  input  [15:0] in_3,
  input  [15:0] in_4,
  output out_5,
  output out_6,
  output out_7,
  output out_8,
  output out_9,
  output out_10,
  output out_11,
  output out_12,
  output out_13,
  output out_14,
  output out_15,
  output out_16,
  output out_17,
  output out_18,
  output out_19,
  output out_20
);

  wire and_1_out, and_2_out, and_3_out, and_4_out, and_5_out, and_6_out, and_7_out, and_8_out, and_9_out,
       and_10_out, and_11_out, and_12_out, and_13_out, and_14_out, and_15_out, and_16_out, and_17_out,
       and_18_out, and_19_out, and_20_out, and_21_out, and_22_out, and_23_out, and_24_out, and_25_out,
       and_26_out, and_27_out, and_28_out, and_29_out, and_30_out, and_31_out, and_32_out, and_33_out,
       and_34_out, and_35_out, and_36_out, and_37_out, and_38_out, and_39_out, and_40_out, and_41_out,
       and_42_out, and_43_out, and_44_out, and_45_out, and_46_out, and_47_out, and_48_out, and_49_out,
       and_50_out, and_51_out, and_52_out, and_53_out, and_54_out, and_55_out, and_56_out, and_57_out,
       and_58_out, and_59_out, and_60_out, and_61_out, and_62_out, and_63_out, and_64_out, and_65_out,
       and_66_out, and_67_out, and_68_out, and_69_out, and_70_out, and_71_out, and_72_out, and_81_out,
       and_82_out, and_83_out, and_84_out, and_85_out, and_86_out, and_87_out, and_88_out, and_89_out,
       and_90_out, and_91_out, and_92_out, and_93_out, and_94_out, and_95_out, and_96_out, and_97_out,
       and_98_out, and_99_out, and_100_out, and_101_out, and_102_out, and_103_out, and_104_out, and_105_out,
       and_106_out, and_107_out, and_108_out, and_109_out, and_110_out, and_111_out, and_112_out,
       and_113_out, and_117_out, and_118_out, and_119_out, and_120_out, and_121_out, and_122_out,
       and_123_out, not_1_out, not_2_out, not_3_out, not_4_out, not_5_out, not_6_out, not_7_out, not_8_out,
       not_9_out, not_10_out, not_11_out, not_12_out, not_13_out, not_14_out, not_15_out, not_16_out,
       not_17_out, not_18_out, not_19_out, not_20_out, not_21_out, not_22_out, not_23_out, not_24_out,
       not_25_out, not_26_out, not_27_out, not_28_out, not_29_out, not_30_out, not_31_out, not_32_out,
       not_33_out, not_34_out, not_35_out, not_36_out, not_37_out, not_38_out, not_39_out, not_40_out,
       not_41_out, not_42_out, not_43_out, not_44_out, not_45_out, not_46_out, not_47_out, not_48_out,
       or_1_out, or_2_out, or_3_out, or_4_out, or_5_out, or_6_out, or_7_out, or_8_out, or_9_out, or_10_out,
       or_11_out, or_12_out, or_13_out, or_14_out, or_15_out, or_16_out, or_17_out, or_18_out, or_19_out,
       or_20_out, or_21_out, or_22_out, or_23_out, or_24_out, or_25_out, or_26_out, or_27_out, or_28_out,
       or_29_out, or_30_out, or_31_out, or_32_out, or_33_out, or_34_out, or_35_out, or_36_out, or_37_out,
       or_38_out, or_39_out, or_40_out, or_41_out, or_42_out, or_43_out, or_44_out, or_45_out, or_46_out,
       or_47_out, or_48_out, or_49_out, or_50_out, or_51_out, or_52_out, or_53_out, or_54_out, or_55_out,
       or_56_out, or_57_out, or_58_out, or_59_out, or_60_out, or_61_out, or_62_out, or_63_out, or_64_out;

  not not_1 (not_1_out, and_1_out);
  and and_1 (and_1_out, in_1, in_4[0]);
  or or_1 (or_1_out, in_4[0], in_1);
  not not_2 (not_2_out, and_2_out);
  and and_2 (and_2_out, in_1, in_4[1]);
  or or_2 (or_2_out, in_4[1], in_1);
  and and_3 (and_3_out, in_1, in_4[2]);
  or or_3 (or_3_out, in_4[2], in_1);
  and and_4 (and_4_out, in_1, in_4[4]);
  or or_4 (or_4_out, in_4[4], in_1);
  and and_5 (and_5_out, in_1, in_4[3]);
  or or_5 (or_5_out, in_4[3], in_1);
  and and_6 (and_6_out, in_1, in_4[5]);
  or or_6 (or_6_out, in_4[5], in_1);
  and and_7 (and_7_out, in_1, in_4[6]);
  or or_7 (or_7_out, in_4[6], in_1);
  and and_8 (and_8_out, in_1, in_4[7]);
  or or_8 (or_8_out, in_4[7], in_1);
  and and_9 (and_9_out, in_1, in_4[8]);
  or or_9 (or_9_out, in_4[8], in_1);
  and and_10 (and_10_out, in_1, in_4[9]);
  or or_10 (or_10_out, in_4[9], in_1);
  and and_11 (and_11_out, in_1, in_4[10]);
  or or_11 (or_11_out, in_4[10], in_1);
  and and_12 (and_12_out, in_1, in_4[11]);
  or or_12 (or_12_out, in_4[11], in_1);
  and and_13 (and_13_out, not_1_out, or_1_out);
  and and_14 (and_14_out, not_2_out, or_2_out);
  not not_3 (not_3_out, and_3_out);
  and and_15 (and_15_out, not_3_out, or_3_out);
  not not_4 (not_4_out, and_4_out);
  and and_16 (and_16_out, not_4_out, or_4_out);
  not not_5 (not_5_out, and_5_out);
  not not_6 (not_6_out, and_6_out);
  not not_7 (not_7_out, and_7_out);
  not not_8 (not_8_out, and_8_out);
  not not_9 (not_9_out, and_9_out);
  not not_10 (not_10_out, and_10_out);
  not not_11 (not_11_out, and_11_out);
  not not_12 (not_12_out, and_12_out);
  and and_17 (and_17_out, in_1, in_4[12]);
  not not_13 (not_13_out, and_17_out);
  or or_13 (or_13_out, in_4[12], in_1);
  and and_18 (and_18_out, in_1, in_4[13]);
  not not_14 (not_14_out, and_18_out);
  or or_14 (or_14_out, in_4[13], in_1);
  and and_19 (and_19_out, in_1, in_4[14]);
  not not_15 (not_15_out, and_19_out);
  or or_15 (or_15_out, in_4[14], in_1);
  not not_16 (not_16_out, and_20_out);
  and and_20 (and_20_out, in_1, in_4[15]);
  or or_16 (or_16_out, in_4[15], in_1);
  and and_21 (and_21_out, not_5_out, or_5_out);
  and and_22 (and_22_out, not_6_out, or_6_out);
  and and_23 (and_23_out, not_7_out, or_7_out);
  and and_24 (and_24_out, not_8_out, or_8_out);
  and and_25 (and_25_out, not_9_out, or_9_out);
  and and_26 (and_26_out, not_10_out, or_10_out);
  and and_27 (and_27_out, not_11_out, or_11_out);
  and and_28 (and_28_out, not_12_out, or_12_out);
  and and_29 (and_29_out, not_13_out, or_13_out);
  and and_30 (and_30_out, not_14_out, or_14_out);
  and and_31 (and_31_out, not_15_out, or_15_out);
  and and_32 (and_32_out, not_16_out, or_16_out);
  and and_33 (and_33_out, in_3[2], and_15_out);
  or or_17 (or_17_out, and_15_out, in_3[2]);
  and and_34 (and_34_out, in_3[2], in_3[2]);
  and and_35 (and_35_out, in_3[4], and_21_out);
  or or_18 (or_18_out, and_21_out, in_3[4]);
  and and_36 (and_36_out, in_3[4], in_3[4]);
  and and_37 (and_37_out, in_3[6], and_23_out);
  or or_19 (or_19_out, and_23_out, in_3[6]);
  and and_38 (and_38_out, in_3[6], in_3[6]);
  not not_17 (not_17_out, and_33_out);
  not not_18 (not_18_out, and_35_out);
  not not_19 (not_19_out, and_37_out);
  and and_39 (and_39_out, in_3[8], and_25_out);
  or or_20 (or_20_out, and_25_out, in_3[8]);
  and and_40 (and_40_out, in_3[8], in_3[8]);
  and and_41 (and_41_out, in_3[10], and_27_out);
  or or_21 (or_21_out, and_27_out, in_3[10]);
  and and_42 (and_42_out, in_3[10], in_3[10]);
  and and_43 (and_43_out, in_3[12], and_29_out);
  not not_20 (not_20_out, and_43_out);
  or or_22 (or_22_out, and_29_out, in_3[12]);
  and and_44 (and_44_out, in_3[12], in_3[12]);
  and and_45 (and_45_out, in_3[14], and_31_out);
  or or_23 (or_23_out, and_31_out, in_3[14]);
  and and_46 (and_46_out, in_3[14], in_3[14]);
  and and_47 (and_47_out, in_3[0], and_13_out);
  not not_21 (not_21_out, and_47_out);
  or or_24 (or_24_out, and_13_out, in_3[0]);
  and and_48 (and_48_out, in_3[0], in_3[0]);
  and and_49 (and_49_out, not_17_out, or_17_out);
  and and_50 (and_50_out, not_18_out, or_18_out);
  and and_51 (and_51_out, not_19_out, or_19_out);
  not not_22 (not_22_out, and_39_out);
  and and_52 (and_52_out, not_22_out, or_20_out);
  not not_23 (not_23_out, and_41_out);
  and and_53 (and_53_out, not_23_out, or_21_out);
  and and_54 (and_54_out, not_20_out, or_22_out);
  not not_24 (not_24_out, and_45_out);
  and and_55 (and_55_out, not_21_out, or_24_out);
  and and_56 (and_56_out, not_24_out, or_23_out);
  and and_57 (and_57_out, and_49_out, or_54_out);
  or or_25 (or_25_out, or_54_out, and_49_out);
  and and_58 (and_58_out, and_50_out, or_55_out);
  or or_26 (or_26_out, or_55_out, and_50_out);
  and and_59 (and_59_out, or_55_out, and_50_out);
  and and_60 (and_60_out, and_51_out, or_60_out);
  or or_27 (or_27_out, or_60_out, and_51_out);
  not not_25 (not_25_out, and_57_out);
  and and_61 (and_61_out, or_54_out, and_49_out);
  not not_26 (not_26_out, and_58_out);
  not not_27 (not_27_out, and_60_out);
  and and_62 (and_62_out, or_60_out, and_51_out);
  and and_63 (and_63_out, and_52_out, or_56_out);
  not not_28 (not_28_out, and_63_out);
  or or_28 (or_28_out, or_56_out, and_52_out);
  and and_64 (and_64_out, or_56_out, and_52_out);
  and and_65 (and_65_out, and_53_out, or_61_out);
  not not_29 (not_29_out, and_65_out);
  or or_29 (or_29_out, or_61_out, and_53_out);
  and and_66 (and_66_out, or_61_out, and_53_out);
  not not_30 (not_30_out, and_67_out);
  and and_67 (and_67_out, and_54_out, or_62_out);
  or or_30 (or_30_out, or_62_out, and_54_out);
  and and_68 (and_68_out, or_62_out, and_54_out);
  and and_69 (and_69_out, and_56_out, or_63_out);
  or or_31 (or_31_out, or_63_out, and_56_out);
  and and_70 (and_70_out, or_63_out, and_56_out);
  not not_31 (not_31_out, and_71_out);
  and and_71 (and_71_out, and_55_out, in_2);
  or or_32 (or_32_out, in_2, and_55_out);
  and and_72 (and_72_out, in_2, and_55_out);
  and and_73 (out_7, not_25_out, or_25_out);
  or or_33 (or_33_out, and_61_out, and_34_out);
  and and_74 (out_9, not_26_out, or_26_out);
  or or_34 (or_34_out, and_59_out, and_36_out);
  and and_75 (out_11, not_27_out, or_27_out);
  or or_35 (or_35_out, and_62_out, and_38_out);
  and and_76 (out_13, not_28_out, or_28_out);
  and and_77 (out_15, not_29_out, or_29_out);
  and and_78 (out_17, not_30_out, or_30_out);
  or or_36 (or_36_out, and_68_out, and_44_out);
  not not_32 (not_32_out, and_69_out);
  and and_79 (out_19, not_32_out, or_31_out);
  and and_80 (out_5, not_31_out, or_32_out);
  or or_37 (or_37_out, and_72_out, and_48_out);
  or or_38 (or_38_out, and_64_out, and_40_out);
  or or_39 (or_39_out, and_66_out, and_42_out);
  or or_40 (or_40_out, and_70_out, and_46_out);
  not not_33 (not_33_out, and_81_out);
  and and_81 (and_81_out, in_3[1], and_14_out);
  or or_41 (or_41_out, and_14_out, in_3[1]);
  and and_82 (and_82_out, in_3[1], in_3[1]);
  not not_34 (not_34_out, and_83_out);
  and and_83 (and_83_out, in_3[3], and_16_out);
  or or_42 (or_42_out, and_16_out, in_3[3]);
  and and_84 (and_84_out, in_3[3], in_3[3]);
  and and_85 (and_85_out, in_3[5], and_22_out);
  or or_43 (or_43_out, and_22_out, in_3[5]);
  and and_86 (and_86_out, in_3[5], in_3[5]);
  and and_87 (and_87_out, in_3[7], and_24_out);
  not not_35 (not_35_out, and_87_out);
  or or_44 (or_44_out, and_24_out, in_3[7]);
  and and_88 (and_88_out, in_3[7], in_3[7]);
  and and_89 (and_89_out, not_33_out, or_41_out);
  and and_90 (and_90_out, not_34_out, or_42_out);
  not not_36 (not_36_out, and_85_out);
  and and_91 (and_91_out, not_35_out, or_44_out);
  and and_92 (and_92_out, in_3[9], and_26_out);
  not not_37 (not_37_out, and_92_out);
  or or_45 (or_45_out, and_26_out, in_3[9]);
  and and_93 (and_93_out, in_3[9], in_3[9]);
  not not_38 (not_38_out, and_94_out);
  and and_94 (and_94_out, in_3[11], and_28_out);
  or or_46 (or_46_out, and_28_out, in_3[11]);
  and and_95 (and_95_out, in_3[11], in_3[11]);
  and and_96 (and_96_out, in_3[13], and_30_out);
  not not_39 (not_39_out, and_96_out);
  or or_47 (or_47_out, and_30_out, in_3[13]);
  and and_97 (and_97_out, in_3[13], in_3[13]);
  and and_98 (and_98_out, in_3[15], and_32_out);
  or or_48 (or_48_out, and_32_out, in_3[15]);
  and and_99 (and_99_out, in_3[15], in_3[15]);
  and and_100 (and_100_out, not_36_out, or_43_out);
  and and_101 (and_101_out, not_37_out, or_45_out);
  and and_102 (and_102_out, not_38_out, or_46_out);
  and and_103 (and_103_out, not_39_out, or_47_out);
  not not_40 (not_40_out, and_98_out);
  and and_104 (and_104_out, not_40_out, or_48_out);
  and and_105 (and_105_out, and_89_out, or_37_out);
  or or_49 (or_49_out, or_37_out, and_89_out);
  and and_106 (and_106_out, and_90_out, or_33_out);
  or or_50 (or_50_out, or_33_out, and_90_out);
  not not_41 (not_41_out, and_105_out);
  and and_107 (and_107_out, or_37_out, and_89_out);
  not not_42 (not_42_out, and_106_out);
  and and_108 (and_108_out, or_33_out, and_90_out);
  and and_109 (and_109_out, and_100_out, or_34_out);
  or or_51 (or_51_out, or_34_out, and_100_out);
  and and_110 (and_110_out, or_34_out, and_100_out);
  not not_43 (not_43_out, and_111_out);
  and and_111 (and_111_out, and_91_out, or_35_out);
  or or_52 (or_52_out, or_35_out, and_91_out);
  and and_112 (and_112_out, or_35_out, and_91_out);
  and and_113 (and_113_out, and_101_out, or_38_out);
  or or_53 (or_53_out, or_38_out, and_101_out);
  and and_114 (out_6, not_41_out, or_49_out);
  or or_54 (or_54_out, and_107_out, and_82_out);
  and and_115 (out_8, not_42_out, or_50_out);
  or or_55 (or_55_out, and_108_out, and_84_out);
  not not_44 (not_44_out, and_109_out);
  and and_116 (out_12, not_43_out, or_52_out);
  or or_56 (or_56_out, and_112_out, and_88_out);
  not not_45 (not_45_out, and_113_out);
  and and_117 (and_117_out, or_38_out, and_101_out);
  not not_46 (not_46_out, and_118_out);
  and and_118 (and_118_out, and_102_out, or_39_out);
  or or_57 (or_57_out, or_39_out, and_102_out);
  and and_119 (and_119_out, or_39_out, and_102_out);
  and and_120 (and_120_out, and_103_out, or_36_out);
  not not_47 (not_47_out, and_120_out);
  or or_58 (or_58_out, or_36_out, and_103_out);
  and and_121 (and_121_out, or_36_out, and_103_out);
  and and_122 (and_122_out, and_104_out, or_40_out);
  not not_48 (not_48_out, and_122_out);
  or or_59 (or_59_out, or_40_out, and_104_out);
  and and_123 (and_123_out, or_40_out, and_104_out);
  and and_124 (out_10, not_44_out, or_51_out);
  or or_60 (or_60_out, and_110_out, and_86_out);
  and and_125 (out_14, not_45_out, or_53_out);
  or or_61 (or_61_out, and_117_out, and_93_out);
  and and_126 (out_16, not_46_out, or_57_out);
  or or_62 (or_62_out, and_119_out, and_95_out);
  and and_127 (out_18, not_47_out, or_58_out);
  or or_63 (or_63_out, and_121_out, and_97_out);
  and and_128 (out_20, not_48_out, or_59_out);
  or or_64 (or_64_out, and_123_out, and_99_out);
endmodule
