// Logisim project NEW_DESIG4_16.circ as structural Verilog: 1 circuit, main circuit main
module main (
  input  in_1,
  input  in_2,
  input  in_3,
  input  in_4,
  input  in_5,
  input  in_6,
  input  in_7,
  input  in_8,
  input  in_9,
  input  in_10,
  input  in_11,
  input  in_12,
  input  in_13,
  input  in_14,
  input  in_15,
  input  in_16,
  input  in_17,
  input  in_18,
  input  in_19,
  input  in_20,
  input  in_21,
  input  in_22,
  input  in_23,
  input  in_24,
  input  in_25,
  input  in_26,
  input  in_27,
  input  in_28,
  input  in_29,
  input  in_30,
  input  in_31,
  input  in_32,
  input  in_33,
  input  in_34,
  input  in_35,
  input  in_36,
  input  in_37,
  input  in_38,
  input  in_39,
  input  in_40,
  input  in_41,
  input  in_42,
  input  in_43,
  input  in_44,
  input  in_45,
  input  in_46,
  input  in_47,
  input  in_48,
  input  in_49,
  input  in_50,
  input  in_51,
  input  in_52,
  input  in_53,
  input  in_54,
  input  in_55,
  input  in_56,
  input  in_57,
  input  in_58,
  input  in_59,
  input  in_60,
  input  in_61,
  input  in_62,
  input  in_63,
  input  in_64,
  input  in_65,
  input  in_66
);

  wire and_1_out, and_2_out, and_3_out, and_4_out, and_5_out, and_6_out, and_7_out, and_8_out, and_9_out,
       and_10_out, and_11_out, and_12_out, and_13_out, and_14_out, and_15_out, and_16_out, and_17_out,
       and_18_out, and_19_out, and_20_out, and_21_out, and_22_out, and_23_out, and_24_out, and_25_out,
       and_26_out, and_27_out, and_28_out, and_29_out, and_30_out, and_31_out, and_32_out, and_33_out,
       and_34_out, and_35_out, and_36_out, and_37_out, and_38_out, and_39_out, and_40_out, and_41_out,
       and_42_out, and_43_out, and_44_out, and_45_out, and_46_out, and_47_out, and_48_out, and_49_out,
       and_50_out, and_51_out, and_52_out, and_53_out, and_54_out, and_55_out, and_56_out, and_57_out,
       and_58_out, and_59_out, and_60_out, and_61_out, and_62_out, and_63_out, and_64_out, not_1_out,
       not_2_out, or_1_out, or_2_out, or_3_out, or_4_out, or_5_out, or_6_out, or_7_out, or_8_out, or_9_out,
       or_10_out, or_11_out, or_12_out, or_13_out, or_14_out, or_15_out, or_16_out;

  LED led_1 (.in(or_1_out));
  LED led_2 (.in(or_2_out));
  LED led_3 (.in(or_3_out));
  LED led_4 (.in(or_5_out));
  LED led_5 (.in(or_4_out));
  LED led_6 (.in(or_6_out));
  not not_1 (not_1_out, in_1);
  LED led_7 (.in(or_8_out));
  LED led_8 (.in(or_7_out));
  LED led_9 (.in(or_9_out));
  LED led_10 (.in(or_12_out));
  LED led_11 (.in(or_11_out));
  LED led_12 (.in(or_10_out));
  not not_2 (not_2_out, in_2);
  LED led_13 (.in(or_14_out));
  LED led_14 (.in(or_13_out));
  LED led_15 (.in(or_16_out));
  LED led_16 (.in(or_15_out));
  or or_1 (or_1_out, and_49_out, and_33_out, and_17_out, and_1_out);
  or or_2 (or_2_out, and_50_out, and_34_out, and_18_out, and_2_out);
  or or_3 (or_3_out, and_51_out, and_35_out, and_19_out, and_3_out);
  or or_4 (or_4_out, and_52_out, and_36_out, and_20_out, and_4_out);
  or or_5 (or_5_out, and_53_out, and_37_out, and_21_out, and_5_out);
  or or_6 (or_6_out, and_54_out, and_38_out, and_22_out, and_6_out);
  or or_7 (or_7_out, and_55_out, and_39_out, and_23_out, and_7_out);
  or or_8 (or_8_out, and_56_out, and_40_out, and_24_out, and_8_out);
  or or_9 (or_9_out, and_57_out, and_41_out, and_25_out, and_9_out);
  or or_10 (or_10_out, and_58_out, and_42_out, and_26_out, and_10_out);
  or or_11 (or_11_out, and_59_out, and_43_out, and_27_out, and_11_out);
  or or_12 (or_12_out, and_60_out, and_44_out, and_28_out, and_12_out);
  or or_13 (or_13_out, and_61_out, and_45_out, and_29_out, and_13_out);
  or or_14 (or_14_out, and_62_out, and_46_out, and_30_out, and_14_out);
  or or_15 (or_15_out, and_63_out, and_47_out, and_31_out, and_15_out);
  or or_16 (or_16_out, and_64_out, and_48_out, and_32_out, and_16_out);
  and and_1 (and_1_out, not_2_out, not_1_out, in_9);
  and and_2 (and_2_out, not_2_out, not_1_out, in_13);
  and and_3 (and_3_out, not_2_out, not_1_out, in_17);
  and and_4 (and_4_out, not_2_out, not_1_out, in_21);
  and and_5 (and_5_out, not_2_out, not_1_out, in_25);
  and and_6 (and_6_out, not_2_out, not_1_out, in_32);
  and and_7 (and_7_out, not_2_out, not_1_out, in_36);
  and and_8 (and_8_out, not_2_out, not_1_out, in_40);
  and and_9 (and_9_out, not_2_out, not_1_out, in_44);
  and and_10 (and_10_out, not_2_out, not_1_out, in_48);
  and and_11 (and_11_out, not_2_out, not_1_out, in_55);
  and and_12 (and_12_out, not_2_out, not_1_out, in_59);
  and and_13 (and_13_out, not_2_out, not_1_out, in_63);
  and and_14 (and_14_out, not_2_out, not_1_out, in_64);
  and and_15 (and_15_out, not_2_out, not_1_out, in_65);
  and and_16 (and_16_out, not_2_out, not_1_out, in_66);
  and and_17 (and_17_out, in_2, not_1_out, in_5);
  and and_18 (and_18_out, in_2, not_1_out, in_8);
  and and_19 (and_19_out, in_2, not_1_out, in_12);
  and and_20 (and_20_out, in_2, not_1_out, in_16);
  and and_21 (and_21_out, in_2, not_1_out, in_20);
  and and_22 (and_22_out, in_2, not_1_out, in_24);
  and and_23 (and_23_out, in_2, not_1_out, in_28);
  and and_24 (and_24_out, in_2, not_1_out, in_31);
  and and_25 (and_25_out, in_2, not_1_out, in_35);
  and and_26 (and_26_out, in_2, not_1_out, in_39);
  and and_27 (and_27_out, in_2, not_1_out, in_43);
  and and_28 (and_28_out, in_2, not_1_out, in_47);
  and and_29 (and_29_out, in_2, not_1_out, in_51);
  and and_30 (and_30_out, in_2, not_1_out, in_54);
  and and_31 (and_31_out, in_2, not_1_out, in_58);
  and and_32 (and_32_out, in_2, not_1_out, in_62);
  and and_33 (and_33_out, not_2_out, in_1, in_4);
  and and_34 (and_34_out, not_2_out, in_1, in_7);
  and and_35 (and_35_out, not_2_out, in_1, in_11);
  and and_36 (and_36_out, not_2_out, in_1, in_15);
  and and_37 (and_37_out, not_2_out, in_1, in_19);
  and and_38 (and_38_out, not_2_out, in_1, in_23);
  and and_39 (and_39_out, not_2_out, in_1, in_27);
  and and_40 (and_40_out, not_2_out, in_1, in_30);
  and and_41 (and_41_out, not_2_out, in_1, in_34);
  and and_42 (and_42_out, not_2_out, in_1, in_38);
  and and_43 (and_43_out, not_2_out, in_1, in_42);
  and and_44 (and_44_out, not_2_out, in_1, in_46);
  and and_45 (and_45_out, not_2_out, in_1, in_50);
  and and_46 (and_46_out, not_2_out, in_1, in_53);
  and and_47 (and_47_out, not_2_out, in_1, in_57);
  and and_48 (and_48_out, not_2_out, in_1, in_61);
  and and_49 (and_49_out, in_2, in_1, in_3);
  and and_50 (and_50_out, in_2, in_1, in_6);
  and and_51 (and_51_out, in_2, in_1, in_10);
  and and_52 (and_52_out, in_2, in_1, in_14);
  and and_53 (and_53_out, in_2, in_1, in_18);
  and and_54 (and_54_out, in_2, in_1, in_22);
  and and_55 (and_55_out, in_2, in_1, in_26);
  and and_56 (and_56_out, in_2, in_1, in_29);
  and and_57 (and_57_out, in_2, in_1, in_33);
  and and_58 (and_58_out, in_2, in_1, in_37);
  and and_59 (and_59_out, in_2, in_1, in_41);
  and and_60 (and_60_out, in_2, in_1, in_45);
  and and_61 (and_61_out, in_2, in_1, in_49);
  and and_62 (and_62_out, in_2, in_1, in_52);
  and and_63 (and_63_out, in_2, in_1, in_56);
  and and_64 (and_64_out, in_2, in_1, in_60);
endmodule
